# Fritzing sketch GardenPi (saved by Fritzing 0.9.2b)
breadboards: 1

parts:
  Arduino_UNO = Arduino Uno (Rev3) - ICSP
  Raspberry_PiB+ = Raspberry Pi B+
  U1 = RELAY [package=relay-t9a]
  U2 = TEMPERATURE-SENSOR [package=to-92]
  U3 = TEMPERATURE-SENSOR [package=to-92]
  U4 = TEMPERATURE-SENSOR [package=to-92]
  Componente1 = Logic Level Converter

nets:
  N1: Arduino_UNO.A0, U3.ADJ
  N2: Arduino_UNO.A1, U4.ADJ
  VCC: Arduino_UNO.5V, U1.NO, U2.VCC, U3.VCC, U4.VCC, Componente1.HV
  GND: Arduino_UNO.GND, Raspberry_PiB+.GND, U1.NC, U2.GND, U3.GND, U4.GND, Componente1.GND
  N3: Arduino_UNO.D0/RX, Componente1.RX_HV
  N4: Arduino_UNO.D1/TX, Componente1.TX_HV
  N5: Arduino_UNO.D3_PWM, U1.MAIN
  N6: Arduino_UNO.D5_PWM, U2.ADJ
  VIN: Arduino_UNO.VIN, Raspberry_PiB+.5V
  3V3: Raspberry_PiB+.3v3, Raspberry_PiB+.3V3, Componente1.LV
  N7: Raspberry_PiB+.GIPO15, Componente1.TX_LV
  N8: Raspberry_PiB+.GIPO14, Componente1.RX_LV
